# Fritzing sketch QC2_adapter_board_ATTiny (saved by Fritzing 0.9.6b)
circuit board: 3.64086cm x 2.70187cm
breadboards: 1

parts:
  Vout = Screw terminal - 2 pins [package=THT]
  R2 = Resistor [tolerance=±5% resistance=2.2k power=0.25 package=THT]
  R1 = Resistor [tolerance=±5% resistance=10k power=0.25 package=THT]
  R4 = Resistor [tolerance=±5% resistance=2.2k power=0.25 package=THT]
  R3 = Resistor [tolerance=±5% resistance=10k power=0.25 package=THT]
  C1 = Electrolytic Capacitor [capacitance=10µF voltage=35V package="100 mil [THT, electrolytic]"]
  USB_in = USB Connectors [package=usb-a-h]
  78L33_(Pattern_Reference) = Voltage Regulator [package=to-92]  # not connected
  78L33 = mystery part, 3 pins [chip_label="3,3V Regulator"]
  U1 = ATTINY13 [package=dip]
  LED1 = LED - 3mm [color="Red (633nm)" current=0.030 package="3 mm [THT]"]
  R7 = Resistor [tolerance=±5% resistance=470 part_number=1/4W power=0.25 package=THT]
  R6 = Resistor [tolerance=±5% resistance=470 part_number=1/4W power=0.25 package=THT]
  R8 = Resistor [tolerance=±5% resistance=1k power=0.25 package=THT]
  R5 = Resistor [tolerance=±5% resistance=10k power=0.25 package=THT]
  J1 = male pin header, 2 pins [form="♂ (male)"]
  Q2 = NPN-Transistor [package="TO92 [THT]"]

nets:
  + Vout: Vout.pin1, USB_in.VBUS, 78L33.pin1, R7.Pin_1, R6.Pin_1, R8.Pin_1
  GND: Vout.pin2, R2.Pin_1, C1.-, USB_in.GND, 78L33.pin2, U1.GND, J1.pin2, Q2.E
  D-: R2.Pin_0, R1.Pin_1, USB_in.D-
  N1: R1.Pin_0, U1.PB2(SCK_ADC1)
  D+: R4.Pin_0, R3.Pin_1, USB_in.D+
  N2: R4.Pin_1, U1.PB0(MOSI)
  N3: R3.Pin_0, U1.PB1(MISO)
  3.3V: C1.+, 78L33.pin3, U1.VCC
  N4: U1.PB3(ADC3), R5.Pin_0
  N5: U1.PB4(ADC2), J1.pin1
  N6: LED1.cathode, R7.Pin_0, R6.Pin_0, Q2.C
  N7: LED1.anode, R8.Pin_0
  N8: R5.Pin_1, Q2.B

notes:
  Rges=235R
